# Fritzing sketch led_clock (saved by Fritzing 0.9.10b)
breadboards: 1

parts:
  Part1 = Arduino Nano (Rev3.0) (ICSP)
  S2 = Round Pushbutton
  S3 = Round Pushbutton
  part = RTC_DS1302_module
  Part2 = Adafruit TSL2561 [part_number="Adafruit #439"]
  R1 = Resistor [tolerance=±5% power=0.25 resistance=3.3k package=THT]
  R2 = Resistor [tolerance=±5% power=0.25 resistance=3.3k package=THT]
  RGB_SMD_LED1 = SMD RGB LED (WS2812) [package=5050]
  RGB_SMD_LED2 = SMD RGB LED (WS2812) [package=5050]

nets:
  GND: Part1.RESET, S2.leg0, S3.leg1, part.GND, Part2.GND
  VSS: Part1.GND, RGB_SMD_LED1.VSS, RGB_SMD_LED2.VSS
  N1: Part1.D3, RGB_SMD_LED2.DIn
  N2: Part1.D12/MISO, RGB_SMD_LED1.DIn
  VCC: Part1.5V, RGB_SMD_LED1.VCC, RGB_SMD_LED1.VDD, RGB_SMD_LED2.VCC, RGB_SMD_LED2.VDD
  N3: Part1.A5, part.CLK, Part2.SCL, R2.Pin_0
  N4: Part1.A4, part.DAT, Part2.SDA, R1.Pin_0
  N5: Part1.A3, S3.leg0
  N6: Part1.A1, S2.leg1
  3V3: Part1.3V3, part.VCC, Part2.VIN, R1.Pin_1, R2.Pin_1

custom parts:
  RTC_DS1302_module: Arduino module DS1302 SPI Real Time Clock
  Adafruit TSL2561: The TSL2561 luminosity sensor is an advanced digital light sensor, ideal for use in a wide range of light situations. Compared to low cost CdS cells, this sensor is more precise, allowing for exact lux calculations and can be configured for different gain/timing ranges to detect light ranges from up to 0.1 - 40,000+ Lux on the fly. The best part of this sensor is that it contains both infrared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
